// Digital circuit AddressUnit.dig as structural Verilog
module AddressUnit (
  input  [31:0] Src0,
  input  [31:0] Immediate,
  input  [31:0] RIP,
  input  Mode,
  output [31:0] Address
);

  wire [31:0] add_1_s, add_2_s;

  Add #(.Bits(32)) add_1 (.a(Src0), .b(Immediate), .c_i(1'b0), .s(add_1_s));  // open: c_o
  Add #(.Bits(32)) add_2 (.a(add_1_s), .b(RIP), .c_i(1'b0), .s(add_2_s));  // open: c_o
  Multiplexer #(.Bits(32)) multiplexer_1 (.sel(Mode), .in_0(add_1_s), .in_1(add_2_s), .out(Address));
endmodule
