// Digital circuit AsyncResetDriver.dig as structural Verilog
module AsyncResetDriver (
  input  Clock,
  input  Reset,
  output ClockOut,
  output ResetOut
);

  wire and_1_out, delay_1_out;

  and and_1 (and_1_out, Clock, ~Reset);  // And
  Delay #(.delayTime(5)) delay_1 (.in(Reset), .out(delay_1_out));
  or or_1 (ClockOut, and_1_out, delay_1_out);

  assign ResetOut = Reset;
endmodule
