// Digital circuit BranchUnit.dig as structural Verilog
module BranchUnit (
  input  [31:0] A,
  input  [31:0] B,
  input  [31:0] Immediate,
  input  [31:0] RIP,
  input  [3:0] Op,
  output LoadRIP,
  output [31:0] NewRIP,
  output [31:0] RegValue,
  output WriteReg
);

  wire comparator_1_eq, comparator_2_eq, comparator_3_gt, comparator_3_lt, comparator_4_eq, comparator_4_gt,
       comparator_4_lt, not_1_out, not_2_out, not_3_out, not_4_out, not_5_out;
  wire [31:0] add_1_s, add_2_s;

  Add #(.Bits(32)) add_1 (.a(A), .b(Immediate), .c_i(1'b0), .s(add_1_s));  // open: c_o
  Add #(.Bits(32)) add_2 (.a(Immediate), .b(RIP), .c_i(1'b0), .s(add_2_s));  // open: c_o
  Add #(.Bits(32)) add_3 (.a(RIP), .b(32'h4), .c_i(1'b0), .s(RegValue));  // open: c_o
  Comparator #(.Bits(4)) comparator_1 (.a(4'b1010), .b(Op), .eq(comparator_1_eq));  // open: gt, lt
  Comparator #(.Bits(4)) comparator_2 (.a(Op), .b(4'b1011), .eq(comparator_2_eq));  // open: gt, lt
  Multiplexer #(.Bits(32)) multiplexer_1 (.sel(comparator_1_eq), .in_0(add_2_s), .in_1(add_1_s), .out(NewRIP));
  Comparator #(.Bits(32), .Signed("true")) comparator_3 (
    .a(A), .b(B), .gt(comparator_3_gt), .lt(comparator_3_lt));  // open: eq
  Comparator #(.Bits(32)) comparator_4 (.a(A), .b(B), .gt(comparator_4_gt), .eq(comparator_4_eq), .lt(comparator_4_lt));
  or or_1 (WriteReg, comparator_1_eq, comparator_2_eq);
  Multiplexer #(.Selector_Bits(4)) multiplexer_2 (
    .sel(Op), .in_0(comparator_3_gt), .in_1(comparator_3_lt), .in_2(comparator_4_gt), .in_3(comparator_4_lt),
    .in_4(not_1_out), .in_5(not_2_out), .in_6(not_3_out), .in_7(not_4_out), .in_8(comparator_4_eq),
    .in_9(not_5_out), .in_10(1'b1), .in_11(1'b1), .in_12(1'b1), .in_13(1'b1), .in_14(1'b1), .in_15(1'b1),
    .out(LoadRIP));
  not not_1 (not_1_out, comparator_3_gt);
  not not_2 (not_2_out, comparator_3_lt);
  not not_3 (not_3_out, comparator_4_gt);
  not not_4 (not_4_out, comparator_4_lt);
  not not_5 (not_5_out, comparator_4_eq);
endmodule
