// Digital circuit BubbleReg.dig as structural Verilog
module BubbleReg (
  input  Data,
  input  Enable,
  input  Clock,
  input  Reset,
  output DataOut
);

  wire multiplexer_1_out, or_1_out;

  Multiplexer multiplexer_1 (.sel(Reset), .in_0(Data), .in_1(1'b1), .out(multiplexer_1_out));
  or or_1 (or_1_out, Enable, Reset);
  Register register_1 (.D(multiplexer_1_out), .C(Clock), .en(or_1_out), .Q(DataOut));
endmodule
