// Digital circuit Bypass.dig as structural Verilog
module Bypass (
  input  [4:0] MemBypassReg,
  input  [31:0] MemBypassValue,
  input  CanMemBypass,
  input  [4:0] WBypassReg,
  input  [31:0] WBypassValue,
  input  [4:0] FileBypassReg,
  input  [31:0] FileBypassValue,
  input  [4:0] Src0,
  input  [31:0] Src0Val,
  input  [4:0] Src1,
  input  [31:0] Src1Val,
  output [31:0] A,
  output [31:0] B,
  output Stall
);

  wire singlebypass_1_stall, singlebypass_2_stall;

  SingleBypass singlebypass_1 (
    .MemBypassReg(MemBypassReg), .MemBypassValue(MemBypassValue), .CanMemBypass(CanMemBypass),
    .WBypassReg(WBypassReg), .WBypassValue(WBypassValue), .FileBypassReg(FileBypassReg),
    .FileBypassValue(FileBypassValue), .RegName(Src0), .Value(Src0Val), .BypassValue(A),
    .Stall(singlebypass_1_stall));
  SingleBypass singlebypass_2 (
    .MemBypassReg(MemBypassReg), .MemBypassValue(MemBypassValue), .CanMemBypass(CanMemBypass),
    .WBypassReg(WBypassReg), .WBypassValue(WBypassValue), .FileBypassReg(FileBypassReg),
    .FileBypassValue(FileBypassValue), .RegName(Src1), .Value(Src1Val), .BypassValue(B),
    .Stall(singlebypass_2_stall));
  or or_1 (Stall, singlebypass_1_stall, singlebypass_2_stall);
endmodule
