// Digital circuit BypassTester.dig as structural Verilog
module BypassTester (
  input  [4:0] ByReg,
  input  [4:0] SrcReg,
  output Bypass
);

  wire comparator_1_eq, or_1_out;

  or or_1 (or_1_out, ByReg[0], ByReg[1], ByReg[2], ByReg[3], ByReg[4]);
  Comparator #(.Bits(5)) comparator_1 (.a(ByReg), .b(SrcReg), .eq(comparator_1_eq));  // open: gt, lt
  and and_1 (Bypass, or_1_out, comparator_1_eq);
endmodule
