// Digital circuit CPU.dig as structural Verilog
module CPU (
  input  [31:0] DataIn,
  input  [31:0] InstructionIn,
  input  Enable,
  input  Clock,
  input  Reset,
  output [31:0] DataOut,
  output [31:0] Address,
  output MemEnable,
  output MemWrite,
  output [1:0] MemSize,
  output [31:0] IAddr,
  output Stalls
);

  wire and_1_out, Clock_t, memory_1_bubbleout, memory_1_canbypass, memory_1_regwrite, Reset_t,
       stagedecode_1_addressmode, stagedecode_1_aluswap, stagedecode_1_branchdelay,
       stagedecode_1_branchdestmode, stagedecode_1_branchmode, stagedecode_1_execmode,
       stagedecode_1_immediatemode, stageexec_1_branchdelayout, stageexec_1_bubbleout, stageexec_1_loadrip,
       stagefetch_1_bubble, stagefetch_1_stalldecode, Stall, writeback_1_writedst;
  wire [1:0] stagedecode_1_memmode, stagedecode_1_memsize, stageexec_1_memmodeout, stageexec_1_memsize;
  wire [3:0] stagedecode_1_condition;
  wire [4:0] memory_1_bypassreg, memory_1_dstout, regfile_1_bypassreg, stagedecode_1_aluop,
       stagedecode_1_dst, stagedecode_1_src0, stagedecode_1_src1, stageexec_1_dstout, writeback_1_bypassreg,
       writeback_1_dstout;
  wire [31:0] memory_1_bypassvalue, regfile_1_a, regfile_1_b, regfile_1_bypassvalue, stagedecode_1_immediate,
       stagedecode_1_ripout, stageexec_1_address, stageexec_1_newrip, stageexec_1_value,
       writeback_1_bypassvalue, writeback_1_dataout;

  and and_1 (and_1_out, Enable, Clock);
  AsyncResetDriver asyncresetdriver_1 (.Clock(and_1_out), .Reset(Reset), .ClockOut(Clock_t), .ResetOut(Reset_t));
  StageFetch stagefetch_1 (
    .BranchDelay(stageexec_1_branchdelayout), .LoadRIP(stageexec_1_loadrip), .NewRIP(stageexec_1_newrip),
    .ExecStall(Stall), .Clock(Clock_t), .Reset(Reset_t), .StallDecode(stagefetch_1_stalldecode),
    .Address(IAddr), .Bubble(stagefetch_1_bubble));
  StageDecode stagedecode_1 (
    .InstructionWord(InstructionIn), .Bubble(stagefetch_1_bubble), .ForceBubble(stagefetch_1_stalldecode),
    .ExecStall(Stall), .RIP(IAddr), .Clock(Clock_t), .Reset(Reset_t), .Dst(stagedecode_1_dst),
    .Src0(stagedecode_1_src0), .Src1(stagedecode_1_src1), .Immediate(stagedecode_1_immediate),
    .RipOut(stagedecode_1_ripout), .BubbleOut(Stalls), .ALUOp(stagedecode_1_aluop),
    .ExecMode(stagedecode_1_execmode), .MemMode(stagedecode_1_memmode),
    .ImmediateMode(stagedecode_1_immediatemode), .MemSize(stagedecode_1_memsize),
    .Condition(stagedecode_1_condition), .AddressMode(stagedecode_1_addressmode),
    .ALUSwap(stagedecode_1_aluswap), .BranchMode(stagedecode_1_branchmode),
    .BranchDestMode(stagedecode_1_branchdestmode), .BranchDelay(stagedecode_1_branchdelay));
  RegFile regfile_1 (
    .Data(writeback_1_dataout), .WriteReg(writeback_1_dstout), .WriteEnable(writeback_1_writedst),
    .Src0(stagedecode_1_src0), .Src1(stagedecode_1_src1), .Clock(Clock_t), .A(regfile_1_a), .B(regfile_1_b),
    .BypassValue(regfile_1_bypassvalue), .BypassReg(regfile_1_bypassreg));
  StageExec stageexec_1 (
    .MemBypassReg(memory_1_bypassreg), .MemBypassValue(memory_1_bypassvalue),
    .CanMemBypass(memory_1_canbypass), .WBypassReg(writeback_1_bypassreg),
    .WBypassValue(writeback_1_bypassvalue), .FileBypassReg(regfile_1_bypassreg),
    .FileBypassValue(regfile_1_bypassvalue), .Dst(stagedecode_1_dst), .Src0(stagedecode_1_src0),
    .Src0Data(regfile_1_a), .Src1(stagedecode_1_src1), .Src1Data(regfile_1_b),
    .Immediate(stagedecode_1_immediate), .RIP(stagedecode_1_ripout), .Bubble(Stalls),
    .ALUOp(stagedecode_1_aluop), .Mode(stagedecode_1_execmode), .MemMode(stagedecode_1_memmode),
    .ImmediateMode(stagedecode_1_immediatemode), .MemSizeIn(stagedecode_1_memsize),
    .Condition(stagedecode_1_condition), .AddressMode(stagedecode_1_addressmode),
    .ALUSwap(stagedecode_1_aluswap), .BranchMode(stagedecode_1_branchmode),
    .BranchDestMode(stagedecode_1_branchdestmode), .BranchDelay(stagedecode_1_branchdelay), .Clock(Clock_t),
    .Reset(Reset_t), .BranchDelayOut(stageexec_1_branchdelayout), .NewRIP(stageexec_1_newrip),
    .LoadRIP(stageexec_1_loadrip), .Value(stageexec_1_value), .Address(stageexec_1_address),
    .MemModeOut(stageexec_1_memmodeout), .DstOut(stageexec_1_dstout), .BubbleOut(stageexec_1_bubbleout),
    .Stall(Stall), .MemSize(stageexec_1_memsize));
  Memory memory_1 (
    .Value(stageexec_1_value), .Address(stageexec_1_address), .Mode(stageexec_1_memmodeout),
    .Dst(stageexec_1_dstout), .Bubble(stageexec_1_bubbleout), .Size(stageexec_1_memsize), .Clock(Clock_t),
    .Reset(Reset_t), .MemDataIn(DataIn), .BypassValue(memory_1_bypassvalue), .BypassReg(memory_1_bypassreg),
    .CanBypass(memory_1_canbypass), .DataOut(DataOut), .AddressOut(Address), .MemEnable(MemEnable),
    .MemWrite(MemWrite), .RegWrite(memory_1_regwrite), .DstOut(memory_1_dstout),
    .BubbleOut(memory_1_bubbleout), .SizeOut(MemSize));
  WriteBack writeback_1 (
    .Data(DataOut), .Dst(memory_1_dstout), .WriteEnable(memory_1_regwrite), .Bubble(memory_1_bubbleout),
    .Clock(Clock_t), .Reset(Reset_t), .BypassValue(writeback_1_bypassvalue),
    .BypassReg(writeback_1_bypassreg), .DataOut(writeback_1_dataout), .DstOut(writeback_1_dstout),
    .WriteDst(writeback_1_writedst));
endmodule
