// Digital circuit ConditionUnit.dig as structural Verilog
module ConditionUnit (
  input  [31:0] A,
  input  [31:0] B,
  input  [3:0] Op,
  output LoadRIP
);

  wire comparator_1_gt, comparator_1_lt, comparator_2_eq, comparator_2_gt, comparator_2_lt, not_1_out,
       not_2_out, not_3_out, not_4_out, not_5_out;

  Comparator #(.Signed("true"), .Bits(32)) comparator_1 (
    .a(A), .b(B), .gt(comparator_1_gt), .lt(comparator_1_lt));  // open: eq
  Comparator #(.Bits(32)) comparator_2 (.a(A), .b(B), .gt(comparator_2_gt), .eq(comparator_2_eq), .lt(comparator_2_lt));
  Multiplexer #(.Selector_Bits(4)) multiplexer_1 (
    .sel(Op), .in_0(comparator_1_gt), .in_1(comparator_1_lt), .in_2(comparator_2_gt), .in_3(comparator_2_lt),
    .in_4(not_1_out), .in_5(not_2_out), .in_6(not_3_out), .in_7(not_4_out), .in_8(comparator_2_eq),
    .in_9(not_5_out), .in_10(1'b1), .in_11(1'b1), .in_12(1'b1), .in_13(1'b1), .in_14(1'b1), .in_15(1'b1),
    .out(LoadRIP));
  not not_1 (not_1_out, comparator_1_gt);
  not not_2 (not_2_out, comparator_1_lt);
  not not_3 (not_3_out, comparator_2_gt);
  not not_4 (not_4_out, comparator_2_lt);
  not not_5 (not_5_out, comparator_2_eq);
endmodule
