// Digital circuit FetchControl.dig as structural Verilog
module FetchControl (
  input  LoadRIP,
  input  ExecStall,
  input  Reset,
  input  BranchDelay,
  output StallDecode,
  output Bubble,
  output StorePC,
  output PCChoice,
  output ZeroPC
);

  wire not_1_out;

  not not_1 (not_1_out, BranchDelay);
  or or_1 (StorePC, ~ExecStall, Reset);  // Or
  and and_1 (StallDecode, not_1_out, LoadRIP);
  and and_2 (Bubble, LoadRIP, not_1_out);

  assign PCChoice = LoadRIP;
  assign ZeroPC = Reset;
endmodule
