// Digital circuit HSyncGen.dig as structural Verilog
module HSyncGen (
  input  [9:0] Column,
  output Blank,
  output Sync
);

  wire comparator_1_lt, comparator_2_lt, comparator_3_lt;

  Comparator #(.Bits(10)) comparator_1 (.a(Column), .b(10'h280), .lt(comparator_1_lt));  // open: gt, eq
  Comparator #(.Bits(10)) comparator_2 (.a(Column), .b(10'h290), .lt(comparator_2_lt));  // open: gt, eq
  Comparator #(.Bits(10)) comparator_3 (.a(Column), .b(10'h2f0), .lt(comparator_3_lt));  // open: gt, eq
  and and_1 (Sync, comparator_3_lt, ~comparator_2_lt);  // And
  not not_1 (Blank, comparator_1_lt);
endmodule
