// Digital circuit MemReadDriver.dig as structural Verilog
module MemReadDriver (
  input  [1:0] AddrLow,
  input  [1:0] Size,
  input  [31:0] DataIn,
  output [31:0] DataOut
);

  wire [5:0] barrelshifter_1_out;
  wire [31:0] barrelshifter_2_out, multiplexer_1_out;

  BarrelShifter #(.Bits(6)) barrelshifter_1 (.in({4'b0000, AddrLow}), .shift(3'b011), .out(barrelshifter_1_out));
  BarrelShifter #(.Bits(32), .direction("right")) barrelshifter_2 (
    .in(DataIn), .shift(barrelshifter_1_out), .out(barrelshifter_2_out));
  Multiplexer #(.Selector_Bits(2), .Bits(32)) multiplexer_1 (
    .sel(Size), .in_0(32'hff), .in_1(32'hffff), .in_2({32{1'b1}}), .in_3({32{1'b1}}), .out(multiplexer_1_out));
  assign DataOut = barrelshifter_2_out & multiplexer_1_out;  // And and_1, 32 bits wide
endmodule
