// Digital circuit MemWriteDriver.dig as structural Verilog
module MemWriteDriver (
  input  [31:0] CPUDataIn,
  input  [31:0] MemDataIn,
  input  [1:0] AddrLow,
  input  [1:0] Size,
  output [31:0] DataOut
);

  wire [5:0] RollAmount;
  wire [31:0] and_1_out, and_2_out, barrelshifter_1_out, multiplexer_1_out, or_1_out, xor_1_out;

  Multiplexer #(.Selector_Bits(2), .Bits(32)) multiplexer_1 (
    .sel(Size), .in_0(32'hff), .in_1(32'hffff), .in_2({32{1'b1}}), .in_3({32{1'b1}}), .out(multiplexer_1_out));
  BarrelShifter #(.Bits(32), .barrelShifterMode("rotate"), .direction("right")) barrelshifter_1 (
    .in(MemDataIn), .shift(RollAmount), .out(barrelshifter_1_out));
  assign and_1_out = multiplexer_1_out & CPUDataIn;  // And and_1, 32 bits wide
  assign and_2_out = multiplexer_1_out & barrelshifter_1_out;  // And and_2, 32 bits wide
  BarrelShifter #(.Bits(6)) barrelshifter_2 (.in({4'b0000, AddrLow}), .shift(3'b011), .out(RollAmount));
  assign xor_1_out = and_2_out ^ barrelshifter_1_out;  // XOr xor_1, 32 bits wide
  assign or_1_out = and_1_out | xor_1_out;  // Or or_1, 32 bits wide
  BarrelShifter #(.Bits(32), .barrelShifterMode("rotate")) barrelshifter_3 (
    .in(or_1_out), .shift(RollAmount), .out(DataOut));
endmodule
