// Digital circuit Memory.dig as structural Verilog
module Memory (
  input  [31:0] Value,
  input  [31:0] Address,
  input  [1:0] Mode,
  input  [4:0] Dst,
  input  Bubble,
  input  [1:0] Size,
  input  Clock,
  input  Reset,
  input  [31:0] MemDataIn,
  output [31:0] BypassValue,
  output [4:0] BypassReg,
  output CanBypass,
  output [31:0] DataOut,
  output [31:0] AddressOut,
  output MemEnable,
  output MemWrite,
  output RegWrite,
  output [4:0] DstOut,
  output BubbleOut,
  output [1:0] SizeOut
);

  wire and_1_out, demultiplexer_1_out_0, demultiplexer_1_out_1, demultiplexer_1_out_3, not_1_out;
  wire [1:0] register_3_q;
  wire [31:0] register_1_q;

  Register #(.Bits(32)) register_1 (.D(Value), .C(Clock), .en(1'b1), .Q(register_1_q));
  Register #(.Bits(32)) register_2 (.D(Address), .C(Clock), .en(1'b1), .Q(AddressOut));
  Register #(.Bits(2)) register_3 (.D(Mode), .C(Clock), .en(1'b1), .Q(register_3_q));
  Register #(.Bits(5)) register_4 (.D(Dst), .C(Clock), .en(1'b1), .Q(DstOut));
  BubbleReg bubblereg_1 (.Data(Bubble), .Enable(1'b1), .Clock(Clock), .Reset(Reset), .DataOut(BubbleOut));
  Register #(.Bits(2)) register_5 (.D(Size), .C(Clock), .en(1'b1), .Q(SizeOut));
  not not_1 (not_1_out, BubbleOut);
  Multiplexer #(.Bits(32), .Selector_Bits(2)) multiplexer_1 (
    .sel(register_3_q), .in_0(register_1_q), .in_1(AddressOut), .in_2(register_1_q), .in_3(MemDataIn),
    .out(BypassValue));
  Demultiplexer #(.Selector_Bits(2)) demultiplexer_1 (
    .sel(register_3_q), .in(not_1_out), .out_0(demultiplexer_1_out_0), .out_1(demultiplexer_1_out_1),
    .out_2(MemWrite), .out_3(demultiplexer_1_out_3));
  or or_1 (MemEnable, demultiplexer_1_out_3, MemWrite);
  nand nand_1 (CanBypass, MemEnable, ~MemWrite);  // NAnd
  or or_2 (RegWrite, demultiplexer_1_out_0, demultiplexer_1_out_1, demultiplexer_1_out_3);
  and and_1 (and_1_out, RegWrite, not_1_out);
  assign BypassReg = and_1_out ? DstOut : 5'bz;  // Driver driver_1
  PullDown #(.Bits(5)) pulldown_1 (.out(BypassReg));

  assign DataOut = BypassValue;

  // Other names for the same wires on the sheet: Dst_t[4:0] = DstOut
endmodule
