// Digital circuit MemoryDriver.dig as structural Verilog
module MemoryDriver (
  input  [31:0] CPUDataIn,
  input  [31:0] AddrIn,
  input  [31:0] MemDataIn,
  input  [31:0] MemIDataIn,
  input  [1:0] Size,
  input  [31:0] IAddrIn,
  output [29:0] AddrOut,
  output [29:0] IAddrOut,
  output [31:0] MemIDataOut,
  output [31:0] WriteDataOut,
  output [31:0] ReadDataOut
);

  MemReadDriver memreaddriver_1 (.AddrLow(AddrIn[1:0]), .Size(Size), .DataIn(MemDataIn), .DataOut(ReadDataOut));
  MemWriteDriver memwritedriver_1 (
    .CPUDataIn(CPUDataIn), .MemDataIn(MemDataIn), .AddrLow(AddrIn[1:0]), .Size(Size), .DataOut(WriteDataOut));

  assign AddrOut = AddrIn[31:2];
  assign IAddrOut = IAddrIn[31:2];
  assign MemIDataOut = MemIDataIn;
endmodule
