// Digital circuit Microcode.dig as structural Verilog
module Microcode (
  input  [5:0] Opcode,
  output [1:0] ALUOp,
  output [1:0] MemMode,
  output [1:0] Condition,
  output ALUSwap,
  output ExecMode,
  output ImmediateMode,
  output MemSize,
  output AddressMode,
  output BranchMode,
  output BranchDestModeMode,
  output BranchDelay
);

  wire and_1_out, and_2_out, and_3_out, and_4_out, and_5_out, and_6_out, and_7_out, and_8_out, and_9_out,
       and_10_out, and_11_out, and_12_out, and_13_out, and_14_out, and_15_out, and_16_out, and_17_out,
       and_18_out, and_20_out, and_21_out, and_22_out, and_23_out, and_24_out, and_25_out, and_26_out,
       and_27_out, and_28_out, and_29_out, and_30_out, and_31_out, and_32_out, and_33_out, and_34_out,
       and_35_out, and_36_out, and_37_out, and_38_out, and_39_out, not_1_out, not_2_out, not_3_out,
       not_4_out, not_5_out, not_6_out;

  not not_1 (not_1_out, Opcode[5]);
  not not_2 (not_2_out, Opcode[4]);
  not not_3 (not_3_out, Opcode[3]);
  not not_4 (not_4_out, Opcode[2]);
  not not_5 (not_5_out, Opcode[1]);
  not not_6 (not_6_out, Opcode[0]);
  and and_1 (and_1_out, Opcode[0], Opcode[1], not_4_out, not_3_out, Opcode[4], Opcode[5]);
  and and_2 (and_2_out, not_6_out, not_5_out, not_4_out, not_3_out, Opcode[5]);
  and and_3 (and_3_out, not_5_out, not_4_out, not_3_out, not_2_out, Opcode[5]);
  and and_4 (and_4_out, Opcode[0], Opcode[1], not_4_out, not_3_out, Opcode[4]);
  and and_5 (and_5_out, not_6_out, not_5_out, not_4_out, not_3_out, Opcode[5]);
  and and_6 (and_6_out, not_4_out, not_3_out, Opcode[4], not_1_out);
  and and_7 (and_7_out, Opcode[2], Opcode[3], Opcode[4], not_1_out);
  and and_8 (and_8_out, not_6_out, not_5_out, Opcode[2], not_3_out, Opcode[4], not_1_out);
  and and_9 (and_9_out, not_6_out, not_5_out, not_4_out, Opcode[3], Opcode[4], not_1_out);
  and and_10 (and_10_out, not_6_out, not_5_out, not_4_out, not_3_out, Opcode[4], Opcode[5]);
  and and_11 (and_11_out, Opcode[0], Opcode[1], not_4_out, not_3_out, Opcode[4], Opcode[5]);
  and and_12 (and_12_out, not_6_out, not_5_out, Opcode[2], not_3_out, Opcode[4], not_1_out);
  and and_13 (and_13_out, Opcode[0], Opcode[1], Opcode[2], not_3_out, Opcode[4], not_1_out);
  and and_14 (and_14_out, not_6_out, not_5_out, not_4_out, Opcode[3], Opcode[4], not_1_out);
  and and_15 (and_15_out, Opcode[0], Opcode[1], Opcode[2], not_3_out, Opcode[4], Opcode[5]);
  and and_16 (and_16_out, Opcode[0], not_5_out, not_4_out, Opcode[3], Opcode[4], Opcode[5]);
  and and_17 (and_17_out, not_6_out, Opcode[1], Opcode[2], not_3_out, Opcode[4], Opcode[5]);
  and and_18 (and_18_out, not_6_out, not_5_out, not_4_out, Opcode[3], Opcode[4], Opcode[5]);
  and and_19 (ALUSwap, Opcode[2], Opcode[3], Opcode[4], not_1_out);
  and and_20 (and_20_out, Opcode[1], not_4_out, Opcode[3], Opcode[4], not_1_out);
  and and_21 (and_21_out, Opcode[1], not_4_out, not_3_out, not_2_out, Opcode[5]);
  and and_22 (and_22_out, Opcode[1], Opcode[2], not_3_out, Opcode[4], Opcode[5]);
  and and_23 (and_23_out, not_5_out, not_4_out, Opcode[3], Opcode[4], Opcode[5]);
  and and_24 (and_24_out, not_5_out, not_4_out, not_3_out, not_2_out, Opcode[5]);
  and and_25 (and_25_out, not_4_out, not_3_out, Opcode[4], not_1_out);
  and and_26 (and_26_out, Opcode[2], Opcode[3], Opcode[4], not_1_out);
  and and_27 (and_27_out, not_6_out, not_5_out, Opcode[2], not_3_out, Opcode[4], not_1_out);
  and and_28 (and_28_out, not_6_out, not_5_out, not_4_out, Opcode[3], Opcode[4], not_1_out);
  and and_29 (and_29_out, not_6_out, not_5_out, Opcode[2], not_3_out, Opcode[4], not_1_out);
  and and_30 (and_30_out, Opcode[0], Opcode[1], Opcode[2], not_3_out, Opcode[4], not_1_out);
  and and_31 (and_31_out, not_6_out, not_5_out, not_4_out, not_3_out, Opcode[4], Opcode[5]);
  and and_32 (and_32_out, Opcode[1], not_4_out, Opcode[3], Opcode[4], not_1_out);
  and and_33 (and_33_out, Opcode[1], not_4_out, not_3_out, not_2_out, Opcode[5]);
  and and_34 (and_34_out, Opcode[1], not_4_out, not_3_out, not_2_out, Opcode[5]);
  and and_35 (and_35_out, Opcode[1], Opcode[2], not_3_out, Opcode[4], Opcode[5]);
  and and_36 (and_36_out, not_5_out, not_4_out, Opcode[3], Opcode[4], Opcode[5]);
  and and_37 (and_37_out, not_6_out, Opcode[1], not_4_out, Opcode[3], Opcode[4], not_1_out);
  and and_38 (and_38_out, Opcode[0], Opcode[1], not_4_out, not_3_out, not_2_out, Opcode[5]);
  and and_39 (and_39_out, not_5_out, not_4_out, Opcode[3], Opcode[4], Opcode[5]);
  or or_1 (ALUOp[1], and_1_out, and_2_out, and_3_out);
  or or_2 (MemMode[0], and_12_out, and_13_out, and_14_out);
  or or_3 (Condition[1], and_15_out, and_16_out);
  or or_4 (Condition[0], and_17_out, and_18_out);
  or or_5 (ImmediateMode, and_24_out, and_25_out, and_26_out);
  or or_6 (MemSize, and_27_out, and_28_out);
  or or_7 (AddressMode, and_29_out, and_30_out, and_31_out);
  or or_8 (BranchMode, and_32_out, and_33_out);
  or or_9 (BranchDestModeMode, and_34_out, and_35_out, and_36_out);
  or or_10 (BranchDelay, and_37_out, and_38_out, and_39_out);
  or or_11 (ALUOp[0], and_4_out, and_5_out, and_6_out, and_7_out);
  or or_12 (MemMode[1], and_8_out, and_9_out, and_10_out, and_11_out);
  or or_13 (ExecMode, and_20_out, and_21_out, and_22_out, and_23_out);

  // Other names for the same wires on the sheet: ALUOp_0 = ALUOp[0]; ALUOp_1 = ALUOp[1]; Condition_0 = Condition[0];
  //   Condition_1 = Condition[1]; MemMode_0 = MemMode[0]; MemMode_1 = MemMode[1]; Opcode_0 = Opcode[0];
  //   Opcode_1 = Opcode[1]; Opcode_2 = Opcode[2]; Opcode_3 = Opcode[3]; Opcode_4 = Opcode[4]; Opcode_5 = Opcode[5]
endmodule
