// Digital circuit ProgLoader.dig as structural Verilog
module ProgLoader (
  input  Clock,
  input  Reset,
  output [13:0] RomAddress,
  output [31:0] MemAddress,
  output Enable
);

  wire asyncresetdriver_1_clockout, asyncresetdriver_1_resetout, counter_1_ovf;

  AsyncResetDriver asyncresetdriver_1 (
    .Clock(Clock), .Reset(Reset), .ClockOut(asyncresetdriver_1_clockout),
    .ResetOut(asyncresetdriver_1_resetout));
  Counter #(.Bits(14)) counter_1 (
    .en(Enable), .C(asyncresetdriver_1_clockout), .clr(asyncresetdriver_1_resetout), .out(RomAddress),
    .ovf(counter_1_ovf));
  RS_FF rs_ff_1 (
    .S(counter_1_ovf), .C(asyncresetdriver_1_clockout), .R(asyncresetdriver_1_resetout), .nQ(Enable));  // open: Q
  assign MemAddress = Enable ? {{16{1'b0}}, RomAddress, 2'b00} : 32'bz;  // Driver driver_1

  // Notes on the sheet:
  //   Clock: Hz: 100
endmodule
