// Digital circuit Ram.dig as structural Verilog
module Ram (
  input  [15:0] Address,
  input  [31:0] Data,
  input  [1:0] Size,
  input  Enable,
  input  Write,
  input  [15:0] InstructionAddress,
  input  IEnable,
  input  Clock,
  output [31:0] DataOut,
  output [31:0] InstructionOut
);

  wire ramdriver_1_l0, ramdriver_1_l1, ramdriver_1_l2, ramdriver_1_l3, ramdriver_1_w0, ramdriver_1_w1,
       ramdriver_1_w2, ramdriver_1_w3;
  wire [5:0] barrelshifter_1_out;
  wire [7:0] barrelshifter_2_out, barrelshifter_2_out_2, barrelshifter_2_out_3, barrelshifter_2_out_4,
       ramdualaccess_1_d1, ramdualaccess_1_d2, ramdualaccess_2_d1, ramdualaccess_2_d2, ramdualaccess_3_d1,
       ramdualaccess_3_d2, ramdualaccess_4_d1, ramdualaccess_4_d2;
  wire [13:0] ramdriver_1_a0, ramdriver_1_a1, ramdriver_1_a2, ramdriver_1_a3, ramdriver_2_a0, ramdriver_2_a1,
       ramdriver_2_a2, ramdriver_2_a3;
  wire [31:0] rambackshifter_1_result, rambackshifter_2_result;

  BarrelShifter #(.Bits(6)) barrelshifter_1 (.in({4'b0000, Address[1:0]}), .shift(3'b011), .out(barrelshifter_1_out));
  BarrelShifter #(.Bits(32), .barrelShifterMode("rotate")) barrelshifter_2 (
    .in(Data), .shift(barrelshifter_1_out),
    .out({barrelshifter_2_out_4, barrelshifter_2_out_3, barrelshifter_2_out_2, barrelshifter_2_out}));
  RamDriver ramdriver_1 (
    .Address(Address), .Size(Size), .Enable(Enable), .Write(Write), .W0(ramdriver_1_w0), .W1(ramdriver_1_w1),
    .W2(ramdriver_1_w2), .W3(ramdriver_1_w3), .L0(ramdriver_1_l0), .L1(ramdriver_1_l1), .L2(ramdriver_1_l2),
    .L3(ramdriver_1_l3), .A0(ramdriver_1_a0), .A1(ramdriver_1_a1), .A2(ramdriver_1_a2), .A3(ramdriver_1_a3));
  RamDriver ramdriver_2 (
    .Address(InstructionAddress), .Size(2'b10), .Enable(1'b1), .Write(1'b0), .A0(ramdriver_2_a0),
    .A1(ramdriver_2_a1), .A2(ramdriver_2_a2), .A3(ramdriver_2_a3));  // open: W0, W1, W2, W3, L0, L1, L2, L3
  RAMDualAccess #(.AddrBits(14), .Bits(8)) ramdualaccess_1 (
    .str(ramdriver_1_w0), .C(Clock), .ld(ramdriver_1_l0), .A1(ramdriver_1_a0), .Din1(barrelshifter_2_out),
    .A2(ramdriver_2_a0), .D1(ramdualaccess_1_d1), .D2(ramdualaccess_1_d2));
  RAMDualAccess #(.AddrBits(14), .Bits(8)) ramdualaccess_2 (
    .str(ramdriver_1_w1), .C(Clock), .ld(ramdriver_1_l1), .A1(ramdriver_1_a1), .Din1(barrelshifter_2_out_2),
    .A2(ramdriver_2_a1), .D1(ramdualaccess_2_d1), .D2(ramdualaccess_2_d2));
  RAMDualAccess #(.AddrBits(14), .Bits(8)) ramdualaccess_3 (
    .str(ramdriver_1_w2), .C(Clock), .ld(ramdriver_1_l2), .A1(ramdriver_1_a2), .Din1(barrelshifter_2_out_3),
    .A2(ramdriver_2_a2), .D1(ramdualaccess_3_d1), .D2(ramdualaccess_3_d2));
  RAMDualAccess #(.AddrBits(14), .Bits(8)) ramdualaccess_4 (
    .str(ramdriver_1_w3), .C(Clock), .ld(ramdriver_1_l3), .A1(ramdriver_1_a3), .Din1(barrelshifter_2_out_4),
    .A2(ramdriver_2_a3), .D1(ramdualaccess_4_d1), .D2(ramdualaccess_4_d2));
  RamBackshifter rambackshifter_1 (
    .D0(ramdualaccess_1_d1), .D1(ramdualaccess_2_d1), .D2(ramdualaccess_3_d1), .D3(ramdualaccess_4_d1),
    .Size(Size), .Address(Address), .Result(rambackshifter_1_result));
  RamBackshifter rambackshifter_2 (
    .D0(ramdualaccess_1_d2), .D1(ramdualaccess_2_d2), .D2(ramdualaccess_3_d2), .D3(ramdualaccess_4_d2),
    .Size(2'b10), .Address(InstructionAddress), .Result(rambackshifter_2_result));
  assign DataOut = Enable ? rambackshifter_1_result : 32'bz;  // Driver driver_1
  assign InstructionOut = IEnable ? rambackshifter_2_result : 32'bz;  // Driver driver_2

  // Other names for the same wires on the sheet: IAddr[15:0] = InstructionAddress
endmodule
