// Digital circuit RamBackshifter.dig as structural Verilog
module RamBackshifter (
  input  [7:0] D0,
  input  [7:0] D1,
  input  [7:0] D2,
  input  [7:0] D3,
  input  [1:0] Size,
  input  [15:0] Address,
  output [31:0] Result
);

  wire [5:0] barrelshifter_1_out;
  wire [31:0] barrelshifter_2_out, multiplexer_1_out;

  Multiplexer #(.Selector_Bits(2), .Bits(32)) multiplexer_1 (
    .sel(Size), .in_0(32'hff), .in_1(32'hffff), .in_2({32{1'b1}}), .in_3({32{1'b0}}), .out(multiplexer_1_out));
  BarrelShifter #(.Bits(6)) barrelshifter_1 (.in({4'b0000, Address[1:0]}), .shift(3'b011), .out(barrelshifter_1_out));
  BarrelShifter #(.barrelShifterMode("rotate"), .Bits(32), .direction("right")) barrelshifter_2 (
    .in({D3, D2, D1, D0}), .shift(barrelshifter_1_out), .out(barrelshifter_2_out));
  assign Result = barrelshifter_2_out & multiplexer_1_out;  // And and_1, 32 bits wide
endmodule
