// Digital circuit RamDriver.dig as structural Verilog
module RamDriver (
  input  [15:0] Address,
  input  [1:0] Size,
  input  Enable,
  input  Write,
  output W0,
  output W1,
  output W2,
  output W3,
  output L0,
  output L1,
  output L2,
  output L3,
  output [13:0] A0,
  output [13:0] A1,
  output [13:0] A2,
  output [13:0] A3
);

  wire decoder_1_out_1, decoder_1_out_2, decoder_1_out_3, demultiplexer_1_out_0, demultiplexer_1_out_1,
       or_3_out, or_4_out;
  wire [3:0] barrelshifter_1_out, demultiplexer_1_out_2;

  Demultiplexer #(.Selector_Bits(2)) demultiplexer_1 (
    .sel(Size), .in(Enable), .out_0(demultiplexer_1_out_0), .out_1(demultiplexer_1_out_1),
    .out_2(demultiplexer_1_out_2[3]));  // open: out_3
  Decoder #(.Selector_Bits(2)) decoder_1 (
    .sel(Address[1:0]), .out_1(decoder_1_out_1), .out_2(decoder_1_out_2), .out_3(decoder_1_out_3));  // open: out_0
  or or_1 (demultiplexer_1_out_2[0], demultiplexer_1_out_0, demultiplexer_1_out_1, demultiplexer_1_out_2[3]);
  or or_2 (demultiplexer_1_out_2[1], demultiplexer_1_out_1, demultiplexer_1_out_2[3]);
  or or_3 (or_3_out, decoder_1_out_1, decoder_1_out_2, decoder_1_out_3);
  or or_4 (or_4_out, decoder_1_out_2, decoder_1_out_3);
  Add #(.Bits(14)) add_1 (.a(Address[15:2]), .b({14{1'b0}}), .c_i(or_3_out), .s(A0));  // open: c_o
  Add #(.Bits(14)) add_2 (.a(Address[15:2]), .b({14{1'b0}}), .c_i(or_4_out), .s(A1));  // open: c_o
  Add #(.Bits(14)) add_3 (.a(Address[15:2]), .b({14{1'b0}}), .c_i(decoder_1_out_3), .s(A2));  // open: c_o
  Add #(.Bits(14)) add_4 (.a(Address[15:2]), .b({14{1'b0}}), .c_i(1'b0), .s(A3));  // open: c_o
  BarrelShifter #(.Bits(4), .barrelShifterMode("rotate")) barrelshifter_1 (
    .in({{2{demultiplexer_1_out_2[3]}}, demultiplexer_1_out_2[1:0]}), .shift({1'b0, Address[1:0]}),
    .out(barrelshifter_1_out));
  and and_1 (L0, barrelshifter_1_out[0], ~Write);  // And
  and and_2 (L1, barrelshifter_1_out[1], ~Write);  // And
  and and_3 (L2, barrelshifter_1_out[2], ~Write);  // And
  and and_4 (L3, barrelshifter_1_out[3], ~Write);  // And
  and and_5 (W0, barrelshifter_1_out[0], Write);
  and and_6 (W1, barrelshifter_1_out[1], Write);
  and and_7 (W2, barrelshifter_1_out[2], Write);
  and and_8 (W3, barrelshifter_1_out[3], Write);
endmodule
