// Digital circuit RegFile.dig as structural Verilog
module RegFile (
  input  [31:0] Data,
  input  [4:0] WriteReg,
  input  WriteEnable,
  input  [4:0] Src0,
  input  [4:0] Src1,
  input  Clock,
  output [31:0] A,
  output [31:0] B,
  output [31:0] BypassValue,
  output [4:0] BypassReg
);

  wire or_1_out, or_2_out;
  wire [4:0] multiplexer_1_out;
  wire [31:0] registerfile_1_da, registerfile_1_db;

  Multiplexer #(.Bits(5)) multiplexer_1 (.sel(WriteEnable), .in_0({5{1'b0}}), .in_1(WriteReg), .out(multiplexer_1_out));
  RegisterFile #(.AddrBits(5), .Bits(32)) registerfile_1 (
    .Din(Data), .we(WriteEnable), .Rw(WriteReg), .C(Clock), .Ra(Src0), .Rb(Src1), .Da(registerfile_1_da),
    .Db(registerfile_1_db));
  Register #(.Bits(32)) LastWrittenValue (.D(Data), .C(Clock), .en(1'b1), .Q(BypassValue));
  Register #(.Bits(5)) LastWrittenReg (.D(multiplexer_1_out), .C(Clock), .en(1'b1), .Q(BypassReg));
  or or_1 (or_1_out, Src0[0], Src0[1], Src0[2], Src0[3], Src0[4]);
  or or_2 (or_2_out, Src1[0], Src1[1], Src1[2], Src1[3], Src1[4]);
  assign A = or_1_out ? registerfile_1_da : 32'bz;  // Driver driver_1
  assign B = or_2_out ? registerfile_1_db : 32'bz;  // Driver driver_2
  PullDown #(.Bits(32)) pulldown_1 (.out(A));
  PullDown #(.Bits(32)) pulldown_2 (.out(B));
endmodule
