// Digital circuit SingleBypass.dig as structural Verilog
module SingleBypass (
  input  [4:0] MemBypassReg,
  input  [31:0] MemBypassValue,
  input  CanMemBypass,
  input  [4:0] WBypassReg,
  input  [31:0] WBypassValue,
  input  [4:0] FileBypassReg,
  input  [31:0] FileBypassValue,
  input  [4:0] RegName,
  input  [31:0] Value,
  output [31:0] BypassValue,
  output Stall
);

  wire bypasstester_1_bypass, bypasstester_2_bypass, bypasstester_3_bypass;
  wire [31:0] multiplexer_2_out, multiplexer_3_out;

  BypassTester bypasstester_1 (.ByReg(MemBypassReg), .SrcReg(RegName), .Bypass(bypasstester_1_bypass));
  BypassTester bypasstester_2 (.ByReg(WBypassReg), .SrcReg(RegName), .Bypass(bypasstester_2_bypass));
  BypassTester bypasstester_3 (.ByReg(FileBypassReg), .SrcReg(RegName), .Bypass(bypasstester_3_bypass));
  and and_1 (Stall, bypasstester_1_bypass, ~CanMemBypass);  // And
  Multiplexer #(.Bits(32)) multiplexer_1 (
    .sel(bypasstester_1_bypass), .in_0(multiplexer_2_out), .in_1(MemBypassValue), .out(BypassValue));
  Multiplexer #(.Bits(32)) multiplexer_2 (
    .sel(bypasstester_2_bypass), .in_0(multiplexer_3_out), .in_1(WBypassValue), .out(multiplexer_2_out));
  Multiplexer #(.Bits(32)) multiplexer_3 (
    .sel(bypasstester_3_bypass), .in_0(Value), .in_1(FileBypassValue), .out(multiplexer_3_out));
endmodule
