// Digital circuit StageDecode.dig as structural Verilog
module StageDecode (
  input  [31:0] InstructionWord,
  input  Bubble,
  input  ForceBubble,
  input  ExecStall,
  input  [31:0] RIP,
  input  Clock,
  input  Reset,
  output [4:0] Dst,
  output [4:0] Src0,
  output [4:0] Src1,
  output [31:0] Immediate,
  output [31:0] RipOut,
  output BubbleOut,
  output [4:0] ALUOp,
  output ExecMode,
  output [1:0] MemMode,
  output ImmediateMode,
  output [1:0] MemSize,
  output [3:0] BranchOp,
  output AddressMode
);

  wire bubblereg_1_dataout, not_1_out;
  wire [1:0] IWord_q, IWord_q_3;
  wire [2:0] IWord_q_4;
  wire [6:2] IWord_q_2;
  wire [9:0] Microcode_out;
  wire [11:5] IWord_q_5;
  wire [31:0] bitextender_1_out, bitextender_2_out, bitextender_3_out;

  not not_1 (not_1_out, ExecStall);
  Register #(.Bits(32)) IWord (
    .D(InstructionWord), .C(Clock), .en(not_1_out),
    .Q({IWord_q_5, IWord_q_4, Src1, Src0, Dst, IWord_q_2[6], IWord_q_3, IWord_q_2[3:2], IWord_q}));
  BubbleReg bubblereg_1 (
    .Data(Bubble), .Enable(not_1_out), .Clock(Clock), .Reset(Reset), .DataOut(bubblereg_1_dataout));
  Register #(.Bits(32)) u_RIP (.D(RIP), .C(Clock), .en(not_1_out), .Q(RipOut));
  or or_1 (BubbleOut, bubblereg_1_dataout, ForceBubble);
  // Probe DecodeBubbles on BubbleOut
  LookUpTable #(.Bits(11)) Microcode (
    .in0(IWord_q[0]), .in1(IWord_q[1]), .in2(IWord_q_2[2]), .in3(IWord_q_2[3]), .in4(IWord_q_3[0]),
    .in5(IWord_q_3[1]),
    .out({AddressMode, Microcode_out[9:8], MemSize, ImmediateMode, MemMode, ExecMode, Microcode_out[1:0]}));
  BitExtender #(.inputBits(12), .outputBits(32)) bitextender_1 (
    .in({IWord_q_5, IWord_q_4, Src1[4:3]}), .out(bitextender_1_out));
  BitExtender #(.inputBits(20), .outputBits(32)) bitextender_2 (
    .in({IWord_q_5, IWord_q_4, Src1, Src0}), .out(bitextender_2_out));
  BitExtender #(.inputBits(12), .outputBits(32)) bitextender_3 (.in({IWord_q_5, Dst}), .out(bitextender_3_out));
  Multiplexer #(.Selector_Bits(2), .Bits(5)) multiplexer_1 (
    .sel(Microcode_out[1:0]), .in_0({IWord_q_5[6:5], IWord_q_4}), .in_1({IWord_q, Src1[2:0]}),
    .in_2(5'b00001), .in_3({5{1'b0}}), .out(ALUOp));
  Multiplexer #(.Selector_Bits(2), .Bits(4)) multiplexer_2 (
    .sel(Microcode_out[9:8]), .in_0({1'b0, IWord_q_4}), .in_1({3'b100, IWord_q_4[0]}), .in_2(4'b1010),
    .in_3(4'b1011), .out(BranchOp));
  Multiplexer #(.Selector_Bits(2), .Bits(32)) multiplexer_3 (
    .sel(IWord_q_3), .in_0({32{1'b0}}), .in_1(bitextender_1_out), .in_2(bitextender_2_out),
    .in_3(bitextender_3_out), .out(Immediate));
  // Probe Microcode on {AddressMode, Microcode_out[9:8], MemSize, ImmediateMode, MemMode, ExecMode, Microcode_out[1:0]}
  // Probe Immediate on Immediate
  // Probe ALUOp on ALUOp
  // Probe BranchOp on BranchOp
  // Probe AddressMode on AddressMode
  // Probe ExecMode on ExecMode
  // Probe MemMode on MemMode
  // Probe ImmMode on ImmediateMode
  // Probe MemSize on MemSize

  // Notes on the sheet:
  //   contents of Microcode (hex, n*v repeats v):
  //   16*0,4*21,418,458,498,408,18,58,98,204,4*0,23,22,304,13*0,413
  //   ,453,493,13,53,93,4,104
endmodule
