// Digital circuit StageFetch.dig as structural Verilog
module StageFetch (
  input  LoadRIP,
  input  [31:0] NewRIP,
  input  ExecStall,
  input  Clock,
  input  Reset,
  output LoadsRIP,
  output [31:0] Address,
  output Bubble
);

  wire and_1_out, and_2_out, not_1_out, or_1_out, or_3_out;
  wire [31:0] add_1_s, multiplexer_1_out, multiplexer_2_out;

  not not_1 (not_1_out, ExecStall);
  // Probe LoadRIP on LoadRIP
  // Probe NewRIP on NewRIP
  and and_1 (and_1_out, ~1'b0, not_1_out);  // And
  and and_2 (and_2_out, not_1_out, LoadRIP);
  or or_1 (or_1_out, and_1_out, and_2_out);
  Multiplexer #(.Bits(32)) multiplexer_1 (.sel(LoadRIP), .in_0(add_1_s), .in_1(NewRIP), .out(multiplexer_1_out));
  and and_3 (LoadsRIP, LoadRIP, or_1_out);
  Multiplexer #(.Bits(32)) multiplexer_2 (
    .sel(Reset), .in_0(multiplexer_1_out), .in_1({32{1'b0}}), .out(multiplexer_2_out));
  or or_2 (Bubble, ~or_1_out, LoadRIP);  // Or
  or or_3 (or_3_out, or_1_out, Reset);
  Register #(.Bits(32), .isProgramCounter("true")) PC (.D(multiplexer_2_out), .C(Clock), .en(or_3_out), .Q(Address));
  Add #(.Bits(32)) add_1 (.a(32'h4), .b(Address), .c_i(1'b0), .s(add_1_s));  // open: c_o
endmodule
