// Digital circuit VGADriver.dig as structural Verilog
module VGADriver (
  input  [23:0] DataRGB,
  input  WriteData,
  input  Clock,
  output [7:0] R,
  output [7:0] G,
  output [7:0] B,
  output H,
  output V
);

  wire Column_ovf, hsyncgen_1_blank, nor_1_out, vsyncgen_1_blank;
  wire [9:0] Column_out, Row_out;
  wire [18:0] counterpreset_1_out, PixelAddr;
  wire [23:0] ramdualaccess_1_d2;
  wire [37:0] mul_1_mul;

  CounterPreset #(.maxValue(307199), .Bits(19)) counterpreset_1 (
    .en(WriteData), .C(Clock), .dir(1'b0), .in({19{1'b0}}), .ld(1'b0), .clr(1'b0), .out(counterpreset_1_out));  // open: ovf
  RAMDualAccess #(.AddrBits(19), .Bits(24)) ramdualaccess_1 (
    .str(WriteData), .C(Clock), .ld(1'b0), .A1(counterpreset_1_out), .Din1(DataRGB), .A2(PixelAddr),
    .D2(ramdualaccess_1_d2));  // open: D1
  CounterPreset #(.maxValue(799), .Bits(10)) Column (
    .en(1'b1), .C(Clock), .dir(1'b0), .in({10{1'b0}}), .ld(1'b0), .clr(1'b0), .out(Column_out),
    .ovf(Column_ovf));
  CounterPreset #(.maxValue(524), .Bits(10)) Row (
    .en(Column_ovf), .C(Clock), .dir(1'b0), .in({10{1'b0}}), .ld(1'b0), .clr(1'b0), .out(Row_out));  // open: ovf
  HSyncGen hsyncgen_1 (.Column(Column_out), .Blank(hsyncgen_1_blank), .Sync(H));
  VSyncGen vsyncgen_1 (.Row(Row_out), .Blank(vsyncgen_1_blank), .Sync(V));
  Mul #(.Bits(19)) mul_1 (.a({{9{1'b0}}, Row_out}), .b(19'h280), .mul(mul_1_mul));
  Add #(.Bits(19)) add_1 (.a({{9{1'b0}}, Column_out}), .b(mul_1_mul[18:0]), .c_i(1'b0), .s(PixelAddr));  // open: c_o
  nor nor_1 (nor_1_out, hsyncgen_1_blank, vsyncgen_1_blank);
  assign {B, G, R} = nor_1_out ? ramdualaccess_1_d2 : 24'bz;  // Driver driver_1
  PullDown #(.Bits(24)) pulldown_1 (.out({B, G, R}));

  // Notes on the sheet:
  //   Clock: Hz: 100
endmodule
