// Digital circuit VSyncGen.dig as structural Verilog
module VSyncGen (
  input  [9:0] Row,
  output Blank,
  output Sync
);

  wire comparator_1_lt, comparator_2_lt, comparator_3_lt;

  Comparator #(.Bits(10)) comparator_1 (.a(Row), .b(10'h1e0), .lt(comparator_1_lt));  // open: gt, eq
  Comparator #(.Bits(10)) comparator_2 (.a(Row), .b(10'h1eb), .lt(comparator_2_lt));  // open: gt, eq
  Comparator #(.Bits(10)) comparator_3 (.a(Row), .b(10'h1ed), .lt(comparator_3_lt));  // open: gt, eq
  and and_1 (Sync, comparator_3_lt, ~comparator_2_lt);  // And
  not not_1 (Blank, comparator_1_lt);
endmodule
