// Digital circuit WriteBack.dig as structural Verilog
module WriteBack (
  input  [31:0] Data,
  input  [4:0] Dst,
  input  WriteEnable,
  input  Bubble,
  input  Clock,
  input  Reset,
  output [31:0] BypassValue,
  output [4:0] BypassReg,
  output [31:0] DataOut,
  output [4:0] DstOut,
  output WriteDst
);

  wire bubblereg_1_dataout, or_1_out, register_3_q;

  Register #(.Bits(32)) register_1 (.D(Data), .C(Clock), .en(1'b1), .Q(BypassValue));
  Register #(.Bits(5)) register_2 (.D(Dst), .C(Clock), .en(1'b1), .Q(DstOut));
  Register register_3 (.D(WriteEnable), .C(Clock), .en(1'b1), .Q(register_3_q));
  BubbleReg bubblereg_1 (.Data(Bubble), .Enable(1'b1), .Clock(Clock), .Reset(Reset), .DataOut(bubblereg_1_dataout));
  Multiplexer #(.Bits(5)) multiplexer_1 (.sel(or_1_out), .in_0(DstOut), .in_1({5{1'b0}}), .out(BypassReg));
  or or_1 (or_1_out, ~register_3_q, bubblereg_1_dataout);  // Or
  and and_1 (WriteDst, register_3_q, ~bubblereg_1_dataout);  // And

  assign DataOut = BypassValue;
endmodule
