// Digital circuit main.dig as structural Verilog
module main (
  input  Clock
);

  wire addrspacedivider_1_isel, addrspacedivider_1_sel, addrspacedivider_2_isel, addrspacedivider_2_sel,
       addrspacedivider_3_isel, addrspacedivider_3_sel, addrspacedivider_4_isel, addrspacedivider_4_sel,
       and_1_out, Clock_t, ClockMode_out, comparator_1_eq, cpu_1_memenable, cpu_1_memwrite, MemE, MemW,
       not_1_out, PowOnReset_out, progloader_1_enable, Pulse_out, Reset, Reset_out;
  wire [1:0] cpu_1_memsize, CPUSizeOut;
  wire [13:0] progloader_1_romaddress;
  wire [15:0] addrspacedivider_1_addrlow, addrspacedivider_1_iaddrlow, addrspacedivider_1_nextaddrspace,
       addrspacedivider_2_addrlow, addrspacedivider_2_iaddrlow, addrspacedivider_2_nextaddrspace,
       addrspacedivider_3_addrlow, addrspacedivider_3_iaddrlow, addrspacedivider_3_nextaddrspace,
       addrspacedivider_4_addrlow, addrspacedivider_4_iaddrlow;
  wire [31:0] cpu_1_address, cpu_1_dataout, CPUAddrOut, CPUDataOut, CPUIAddrOut, DataIn, InstructionIn,
       progloader_1_memaddress, romdualport_1_d1;

  DipSwitch ClockMode (.out(ClockMode_out));
  Button Pulse (.out(Pulse_out));
  Button u_Reset (.out(Reset_out));
  Reset #(.invertOutput("false")) PowOnReset (.out(PowOnReset_out));
  Multiplexer multiplexer_1 (.sel(ClockMode_out), .in_0(Pulse_out), .in_1(Clock), .out(Clock_t));
  or or_1 (Reset, Reset_out, PowOnReset_out);
  not not_1 (not_1_out, progloader_1_enable);
  CPU cpu_1 (
    .DataIn(DataIn), .InstructionIn(InstructionIn), .Enable(not_1_out), .Clock(Clock_t), .Reset(Reset),
    .DataOut(cpu_1_dataout), .Address(cpu_1_address), .MemEnable(cpu_1_memenable), .MemWrite(cpu_1_memwrite),
    .MemSize(cpu_1_memsize), .IAddr(CPUIAddrOut));  // open: Stalls
  ProgLoader progloader_1 (
    .Clock(Clock_t), .Reset(Reset), .RomAddress(progloader_1_romaddress),
    .MemAddress(progloader_1_memaddress), .Enable(progloader_1_enable));
  Multiplexer #(.Bits(32)) multiplexer_2 (
    .sel(progloader_1_enable), .in_0(cpu_1_dataout), .in_1(romdualport_1_d1), .out(CPUDataOut));
  Multiplexer #(.Bits(32)) multiplexer_3 (
    .sel(progloader_1_enable), .in_0(cpu_1_address), .in_1(progloader_1_memaddress), .out(CPUAddrOut));
  Multiplexer #(.Bits(2)) multiplexer_4 (
    .sel(progloader_1_enable), .in_0(cpu_1_memsize), .in_1(2'b10), .out(CPUSizeOut));
  or or_2 (MemE, progloader_1_enable, cpu_1_memenable);
  or or_3 (MemW, progloader_1_enable, cpu_1_memwrite);
  ROMDualPort #(.AddrBits(14), .isProgramMemory("true"), .Bits(32)) romdualport_1 (
    .A1(progloader_1_romaddress), .s1(1'b1), .A2({14{1'b0}}), .s2(1'b0), .D1(romdualport_1_d1));  // open: D2
  AddrSpaceDivider addrspacedivider_1 (
    .HighAddrSpace({16{1'b0}}), .Addr(CPUAddrOut), .IAddr(CPUIAddrOut), .MemEnable(MemE), .IEnable(1'b1),
    .AddrLow(addrspacedivider_1_addrlow), .Sel(addrspacedivider_1_sel),
    .IAddrLow(addrspacedivider_1_iaddrlow), .ISel(addrspacedivider_1_isel),
    .NextAddrSpace(addrspacedivider_1_nextaddrspace));
  AddrSpaceDivider addrspacedivider_2 (
    .HighAddrSpace(addrspacedivider_1_nextaddrspace), .Addr(CPUAddrOut), .IAddr(CPUIAddrOut),
    .MemEnable(MemE), .IEnable(1'b1), .AddrLow(addrspacedivider_2_addrlow), .Sel(addrspacedivider_2_sel),
    .IAddrLow(addrspacedivider_2_iaddrlow), .ISel(addrspacedivider_2_isel),
    .NextAddrSpace(addrspacedivider_2_nextaddrspace));
  AddrSpaceDivider addrspacedivider_3 (
    .HighAddrSpace(addrspacedivider_2_nextaddrspace), .Addr(CPUAddrOut), .IAddr(CPUIAddrOut),
    .MemEnable(MemE), .IEnable(1'b1), .AddrLow(addrspacedivider_3_addrlow), .Sel(addrspacedivider_3_sel),
    .IAddrLow(addrspacedivider_3_iaddrlow), .ISel(addrspacedivider_3_isel),
    .NextAddrSpace(addrspacedivider_3_nextaddrspace));
  AddrSpaceDivider addrspacedivider_4 (
    .HighAddrSpace(addrspacedivider_3_nextaddrspace), .Addr(CPUAddrOut), .IAddr(CPUIAddrOut),
    .MemEnable(MemE), .IEnable(1'b1), .AddrLow(addrspacedivider_4_addrlow), .Sel(addrspacedivider_4_sel),
    .IAddrLow(addrspacedivider_4_iaddrlow), .ISel(addrspacedivider_4_isel));  // open: NextAddrSpace
  Comparator #(.Bits(32)) comparator_1 (.a(CPUAddrOut), .b({32{1'b1}}), .eq(comparator_1_eq));  // open: gt, lt
  and and_1 (and_1_out, MemW, MemE, comparator_1_eq);
  Ram ram_1 (
    .Address(addrspacedivider_1_addrlow), .Data(CPUDataOut), .Size(CPUSizeOut),
    .Enable(addrspacedivider_1_sel), .Write(MemW), .InstructionAddress(addrspacedivider_1_iaddrlow),
    .IEnable(addrspacedivider_1_isel), .Clock(Clock_t), .DataOut(DataIn), .InstructionOut(InstructionIn));
  Ram ram_2 (
    .Address(addrspacedivider_2_addrlow), .Data(CPUDataOut), .Size(CPUSizeOut),
    .Enable(addrspacedivider_2_sel), .Write(MemW), .InstructionAddress(addrspacedivider_2_iaddrlow),
    .IEnable(addrspacedivider_2_isel), .Clock(Clock_t), .DataOut(DataIn), .InstructionOut(InstructionIn));
  Ram ram_3 (
    .Address(addrspacedivider_3_addrlow), .Data(CPUDataOut), .Size(CPUSizeOut),
    .Enable(addrspacedivider_3_sel), .Write(MemW), .InstructionAddress(addrspacedivider_3_iaddrlow),
    .IEnable(addrspacedivider_3_isel), .Clock(Clock_t), .DataOut(DataIn), .InstructionOut(InstructionIn));
  Ram ram_4 (
    .Address(addrspacedivider_4_addrlow), .Data(CPUDataOut), .Size(CPUSizeOut),
    .Enable(addrspacedivider_4_sel), .Write(MemW), .InstructionAddress(addrspacedivider_4_iaddrlow),
    .IEnable(addrspacedivider_4_isel), .Clock(Clock_t), .DataOut(DataIn), .InstructionOut(InstructionIn));
  Terminal terminal_1 (.D(CPUDataOut), .C(Clock_t), .en(and_1_out));

  // Notes on the sheet:
  //   Clock: Hz: 5000
  //   contents of romdualport_1 (hex, n*v repeats v):
  //   20f21,5ef10,a4fa2,820,18a0,a30900,e12c36,812080,14fa2,811800,812880
  //   ,fffe8022,22,107ef10,21e035,23e235,25e435,3fe635,801800,108a1
  //   ,fb011897,920,a0a0,3c32636,810080,1111a,88fa2,802800,3041090,201a1
  //   ,f8023432,451890,152910,fffd4022,201a1,a0a0,f6023832,c1ef9a,81e91a
  //   ,41e89a,1e81a,105ef10,1f01b,81f380,10221,f4c04217,2444210,2a0
  //   ,1320,a0a0,3c25036,c4035,464210,145290,806080,34fa2,801300,fffe0022
  //   ,807f80,1f01b,1a0,c41836,c41080,143190,ffff4022,801100,803080
  //   ,1f01b,321111,121191,862080,1f01b
endmodule
